// Logisim project O1_GPU.circ as structural Verilog: 2 circuits, main circuit GPU
module GPUCore (
  input  Clock,
  input  Reset,
  input  [7:0] GPLN,
  input  [7:0] GPIN,
  output [3:0] x,
  output [3:0] y,
  output [7:0] Color
);

  wire counter_1_carry, not_1_out;
  wire [7:0] controlled_buffer_1_out;

  Counter counter_1 (
    .clr(Reset), .up(1'b1), .count(1'b1), .clk(Clock), .carry(counter_1_carry), .Q({y, x}));  // open: load, D
  assign controlled_buffer_1_out = not_1_out ? {y, x} : 8'bz;  // Controlled_Buffer controlled_buffer_1
  assign controlled_buffer_1_out = counter_1_carry ? GPLN : 8'bz;  // Controlled_Buffer controlled_buffer_2
  RAM ram_1 (
    .addr(controlled_buffer_1_out), .we(counter_1_carry), .oe(not_1_out), .clk(Clock), .din(GPIN),
    .dout(Color));
  not not_1 (not_1_out, counter_1_carry);
endmodule

module GPU (
  input  Clock,
  input  Reset,
  input  [7:0] GPLNA,
  input  [7:0] GPLNB,
  input  [7:0] GPINA,
  input  [7:0] GPINB,
  input  [7:0] GPLNC,
  input  [7:0] GPLND,
  input  [7:0] GPINC,
  input  [7:0] GPIND,
  output [3:0] GPXA,
  output [3:0] GPXB,
  output [3:0] GPYA,
  output [3:0] GPYB,
  output [7:0] GPCA,
  output [7:0] GPCB,
  output [3:0] GPXC,
  output [3:0] GPXD,
  output [3:0] GPYC,
  output [3:0] GPYD,
  output [7:0] GPCC,
  output [7:0] GPCD
);

  GPUCore gpucore_1 (.Clock(Clock), .Reset(Reset), .GPLN(GPLNA), .GPIN(GPINA), .x(GPXA), .y(GPYA), .Color(GPCA));
  GPUCore gpucore_2 (.Clock(Clock), .Reset(Reset), .GPLN(GPLNC), .GPIN(GPINC), .x(GPXC), .y(GPYC), .Color(GPCC));
  GPUCore gpucore_3 (.Clock(Clock), .Reset(Reset), .GPLN(GPLNB), .GPIN(GPINB), .x(GPXB), .y(GPYB), .Color(GPCB));
  GPUCore gpucore_4 (.Clock(Clock), .Reset(Reset), .GPLN(GPLND), .GPIN(GPIND), .x(GPXD), .y(GPYD), .Color(GPCD));
endmodule
