// Logisim project O4_CPU(V1).circ as structural Verilog: 4 circuits, main circuit main
module main (
);

  wire button_1_out, clock_1_out;
  wire [1:0] cpu_1_gpio, cpu_1_ramio;
  wire [3:0] undriven_3;
  wire [23:0] cpu_1_proc, cpu_1_sroml;
  wire [31:0] cpu_1_exo, cpu_1_gpo, cpu_1_ramin, rom_2_data, undriven, undriven_2;
  wire [55:0] rom_1_data;

  ROM #(.addrWidth(24), .dataWidth(56)) rom_1 (.addr(cpu_1_proc), .data(rom_1_data));
  Button button_1 (.out(button_1_out));
  Clock clock_1 (.out(clock_1_out));
  ROM #(.addrWidth(24), .dataWidth(32)) rom_2 (.addr(cpu_1_sroml), .data(rom_2_data));
  CPU cpu_1 (
    .reset(button_1_out), .RAMOUT(undriven_2), .RAMAmo(undriven_3), .SROMIN(rom_2_data), .clock(clock_1_out),
    .ExI(undriven), .ROMIN(rom_1_data), .PROC(cpu_1_proc), .RAMIN(cpu_1_ramin), .SROML(cpu_1_sroml),
    .GPO(cpu_1_gpo), .ExO(cpu_1_exo), .GPIO(cpu_1_gpio), .RAMIO(cpu_1_ramio));
endmodule

module CPU (
  input  reset,
  input  [31:0] RAMOUT,
  input  [3:0] RAMAmo,
  input  [31:0] SROMIN,
  input  clock,
  input  [31:0] ExI,
  input  [55:0] ROMIN,
  output [23:0] PROC,
  output [31:0] RAMIN,
  output [23:0] SROML,
  output [31:0] GPO,
  output [31:0] ExO,
  output [1:0] GPIO,
  output [1:0] RAMIO
);

  wire alu_1_gel, buffer_1_out, clu_1_out_2, clu_1_out_3, clu_1_out_7, clu_1_out_8, clu_1_out_9,
       clu_1_out_10, clu_1_out_13, clu_1_out_14, clu_1_out_15, clu_1_out_18, clu_1_out_19, clu_1_out_20,
       clu_1_out_21, clu_1_out_22, clu_1_out_23, clu_1_out_24, clu_1_out_25;
  wire [2:0] clu_1_out_6;
  wire [31:0] alu_1_aluout, controlled_buffer_4_out, register_1_q, register_2_q;

  Counter #(.max('hffffff), .width(24)) counter_1 (
    .clr(reset), .load(buffer_1_out), .up(1'b1), .count(1'b1), .clk(clock), .D(RAMOUT[23:0]), .Q(PROC));  // open: carry
  buf buffer_1 (buffer_1_out, clu_1_out_7);
  assign RAMOUT = clu_1_out_19 ? ExI : 32'bz;  // Controlled_Buffer controlled_buffer_1
  assign RAMOUT = clu_1_out_8 ? ROMIN[31:0] : 32'bz;  // Controlled_Buffer controlled_buffer_2
  CLU clu_1 (
    .Instruct(ROMIN[55:32]), .out_2(clu_1_out_2), .out_3(clu_1_out_3), .out_4(clu_1_out_6[2]),
    .out_5(clu_1_out_6[1]), .out_6(clu_1_out_6[0]), .out_7(clu_1_out_7), .out_8(clu_1_out_8),
    .out_9(clu_1_out_9), .out_10(clu_1_out_10), .out_11(GPIO[0]), .out_12(GPIO[1]), .out_13(clu_1_out_13),
    .out_14(clu_1_out_14), .out_15(clu_1_out_15), .out_16(RAMIO[0]), .out_17(RAMIO[1]),
    .out_18(clu_1_out_18), .out_19(clu_1_out_19), .out_20(clu_1_out_20), .out_21(clu_1_out_21),
    .out_22(clu_1_out_22), .out_23(clu_1_out_23), .out_24(clu_1_out_24), .out_25(clu_1_out_25));
  assign RAMOUT = clu_1_out_14 ? SROMIN : 32'bz;  // Controlled_Buffer controlled_buffer_3
  // Buzzer #(.vol_width(1), .waveform("Square")) buzzer_1: pin names not known; wires that end beside it: clu_1_out_25, clu_1_out_24, clu_1_out_23, clu_1_out_22, {14{1'b1}}, clu_1_out_21, clu_1_out_21
  assign controlled_buffer_4_out = clu_1_out_15 ? RAMOUT : 32'bz;  // Controlled_Buffer controlled_buffer_4
  assign GPO = clu_1_out_13 ? RAMOUT : 32'bz;  // Controlled_Buffer controlled_buffer_5
  Register #(.width(32)) register_1 (.D(RAMOUT), .en(clu_1_out_2), .clk(clock), .Q(register_1_q), .clr(reset));
  Register #(.width(32)) register_2 (.D(RAMOUT), .en(clu_1_out_3), .clk(clock), .Q(register_2_q), .clr(reset));
  assign RAMOUT[31:28] = clu_1_out_18 ? RAMAmo : 4'bz;  // Controlled_Buffer controlled_buffer_6
  Register #(.width(24)) register_3 (
    .D(controlled_buffer_4_out[31:8]), .en(clu_1_out_15), .clk(clock), .Q(SROML), .clr(reset));
  assign ExO = clu_1_out_20 ? RAMOUT : 32'bz;  // Controlled_Buffer controlled_buffer_7
  assign buffer_1_out = clu_1_out_10 ? alu_1_gel : 1'bz;  // Controlled_Buffer controlled_buffer_8
  assign RAMOUT = clu_1_out_9 ? alu_1_aluout : 32'bz;  // Controlled_Buffer controlled_buffer_9
  ALU alu_1 (.A(register_1_q), .B(register_2_q), .Sel(clu_1_out_6), .ALUOut(alu_1_aluout), .GEL(alu_1_gel));

  assign RAMIN = RAMOUT;

  // Notes on the sheet:
  //   non-standard bits
endmodule

module ALU (
  input  [31:0] A,
  input  [31:0] B,
  input  [2:0] Sel,
  output [31:0] ALUOut,
  output GEL
);

  wire comparator_1_eq, comparator_1_gt, comparator_1_lt, decoder_1_out2, decoder_1_out3, decoder_1_out4,
       decoder_1_out5, decoder_1_out6, decoder_1_out7;
  wire [31:0] adder_1_out, multiplier_1_out, subtractor_1_out;

  Decoder #(.select(3)) decoder_1 (
    .out2(decoder_1_out2), .out3(decoder_1_out3), .out4(decoder_1_out4), .out5(decoder_1_out5),
    .out6(decoder_1_out6), .out7(decoder_1_out7), .sel(Sel));  // open: out0, out1, en
  Adder #(.width(32)) adder_1 (.a(A), .b(B), .out(adder_1_out));  // open: cin, cout
  Subtractor #(.width(32)) subtractor_1 (.a(A), .b(B), .out(subtractor_1_out));  // open: bin, bout
  assign ALUOut = decoder_1_out2 ? adder_1_out : 32'bz;  // Controlled_Buffer controlled_buffer_1
  Multiplier #(.width(32)) multiplier_1 (.a(A), .b(B), .out(multiplier_1_out));  // open: cin, cout
  assign ALUOut = decoder_1_out3 ? subtractor_1_out : 32'bz;  // Controlled_Buffer controlled_buffer_2
  assign ALUOut = decoder_1_out4 ? multiplier_1_out : 32'bz;  // Controlled_Buffer controlled_buffer_3
  Comparator #(.width(32)) comparator_1 (
    .a(A), .b(B), .gt(comparator_1_gt), .eq(comparator_1_eq), .lt(comparator_1_lt));
  assign GEL = decoder_1_out6 ? comparator_1_gt : 1'bz;  // Controlled_Buffer controlled_buffer_4
  assign GEL = decoder_1_out7 ? comparator_1_eq : 1'bz;  // Controlled_Buffer controlled_buffer_5
  assign GEL = decoder_1_out5 ? comparator_1_lt : 1'bz;  // Controlled_Buffer controlled_buffer_6
endmodule

module CLU (
  input  [23:0] Instruct,
  output out_2,
  output out_3,
  output out_4,
  output out_5,
  output out_6,
  output out_7,
  output out_8,
  output out_9,
  output out_10,
  output out_11,
  output out_12,
  output out_13,
  output out_14,
  output out_15,
  output out_16,
  output out_17,
  output out_18,
  output out_19,
  output out_20,
  output out_21,
  output out_22,
  output out_23,
  output out_24,
  output out_25
);


  assign out_2 = Instruct[0];
  assign out_3 = Instruct[1];
  assign out_4 = Instruct[2];
  assign out_5 = Instruct[3];
  assign out_6 = Instruct[4];
  assign out_7 = Instruct[5];
  assign out_8 = Instruct[6];
  assign out_9 = Instruct[7];
  assign out_10 = Instruct[8];
  assign out_11 = Instruct[9];
  assign out_12 = Instruct[10];
  assign out_13 = Instruct[11];
  assign out_14 = Instruct[12];
  assign out_15 = Instruct[13];
  assign out_16 = Instruct[14];
  assign out_17 = Instruct[15];
  assign out_18 = Instruct[16];
  assign out_19 = Instruct[17];
  assign out_20 = Instruct[18];
  assign out_21 = Instruct[19];
  assign out_22 = Instruct[20];
  assign out_23 = Instruct[21];
  assign out_24 = Instruct[22];
  assign out_25 = Instruct[23];
endmodule
