// Logisim project O5_CPU.circ as structural Verilog: 4 circuits, main circuit main
module main (
);


  // Notes on the sheet:
  //   No examples here
endmodule

module CPU (
  input  [31:0] RAMIN,
  input  [31:0] EXINA,
  input  [31:0] EXINB,
  input  RESET,
  input  CLOCK,
  input  [24:0] ICLL,
  input  [63:0] ICLD,
  output [31:0] RAMOUT,
  output [23:0] RAMLOC,
  output [23:0] GPC,
  output [31:0] EXINC,
  output [31:0] EXIND,
  output [1:0] RAMIO,
  output [1:0] GPIO
);

  wire clu_1_aluout, clu_1_exina, clu_1_exinb, clu_1_exinc, clu_1_exind, clu_1_numio, clu_1_procl,
       clu_1_regawr, clu_1_regbwr, comparator_1_eq, controlled_buffer_6_out, not_1_out;
  wire [1:0] alu_1_gelout, clu_1_gelsela, clu_1_msela;
  wire [23:0] controlled_buffer_1_out, counter_1_q;
  wire [31:0] A_q, alu_1_mout, B_q;
  wire [63:0] InstructCache_dout;

  Counter #(.max('hffffff), .width(24)) counter_1 (
    .clr(RESET), .load(controlled_buffer_6_out), .up(1'b1), .count(not_1_out), .clk(CLOCK), .D(RAMIN[23:0]),
    .Q(counter_1_q));  // open: carry
  not not_1 (not_1_out, ICLL[24]);
  assign controlled_buffer_1_out = not_1_out ? counter_1_q : 24'bz;  // Controlled_Buffer controlled_buffer_1
  assign controlled_buffer_1_out = ICLL[24] ? ICLL[23:0] : 24'bz;  // Controlled_Buffer controlled_buffer_2
  RAM #(.addrWidth(24), .dataWidth(64)) InstructCache (
    .addr(controlled_buffer_1_out), .we(ICLL[24]), .oe(not_1_out), .clk(CLOCK), .din(ICLD),
    .dout(InstructCache_dout));
  assign RAMIN = clu_1_exina ? EXINA : 32'bz;  // Controlled_Buffer controlled_buffer_3
  assign RAMIN = clu_1_exinb ? EXINB : 32'bz;  // Controlled_Buffer controlled_buffer_4
  assign RAMIN = clu_1_exind ? EXIND : 32'bz;  // Controlled_Buffer controlled_buffer_5
  assign controlled_buffer_6_out = clu_1_procl ? 1'b1 : 1'bz;  // Controlled_Buffer controlled_buffer_6
  assign RAMIN = clu_1_exinc ? EXINC : 32'bz;  // Controlled_Buffer controlled_buffer_7
  Register #(.width(32)) A (.D(RAMIN), .en(clu_1_regbwr), .clk(CLOCK), .Q(A_q), .clr(RESET));
  assign RAMIN = clu_1_numio ? InstructCache_dout[31:0] : 32'bz;  // Controlled_Buffer controlled_buffer_8
  assign controlled_buffer_6_out = comparator_1_eq ? 1'b1 : 1'bz;  // Controlled_Buffer controlled_buffer_9
  Register #(.width(32)) B (.D(RAMIN), .en(clu_1_regawr), .clk(CLOCK), .Q(B_q), .clr(RESET));
  CLU clu_1 (
    .Ins(InstructCache_dout[63:32]), .NumIO(clu_1_numio), .RegAWR(clu_1_regawr), .RegBWR(clu_1_regbwr),
    .MSELA(clu_1_msela[0]), .MSELB(clu_1_msela[1]), .GELSELA(clu_1_gelsela[0]), .GELSELB(clu_1_gelsela[1]),
    .ALUOUT(clu_1_aluout), .PROCL(clu_1_procl), .RAMIOA(RAMIO[0]), .RAMIOB(RAMIO[1]), .GPIOA(GPIO[0]),
    .GPIOB(GPIO[1]), .EXINA(clu_1_exina), .EXINB(clu_1_exinb), .EXINC(clu_1_exinc), .EXIND(clu_1_exind));  // open: out_19, out_20, out_21, out_22, out_23, out_24, out_25, out_26, out_27, out_28, out_29, out_30, out_31, out_32, out_33
  Comparator #(.width(2)) comparator_1 (.a(clu_1_gelsela), .b(alu_1_gelout), .eq(comparator_1_eq));  // open: gt, lt
  assign RAMIN = clu_1_aluout ? alu_1_mout : 32'bz;  // Controlled_Buffer controlled_buffer_10
  ALU alu_1 (.MSEL(clu_1_msela), .A(A_q), .B(B_q), .GELSEL(clu_1_gelsela), .MOUT(alu_1_mout), .GELOUT(alu_1_gelout));

  assign GPC = RAMIN[23:0];
  assign RAMLOC = RAMIN[23:0];
  assign RAMOUT = RAMIN;
endmodule

module ALU (
  input  [1:0] MSEL,
  input  [31:0] A,
  input  [31:0] B,
  input  [1:0] GELSEL,
  output [31:0] MOUT,
  output [1:0] GELOUT
);

  wire comparator_1_eq, comparator_1_gt, comparator_1_lt, decoder_1_out1, decoder_1_out2, decoder_1_out3,
       decoder_2_out0, decoder_2_out1, decoder_2_out2, decoder_2_out3;
  wire [1:0] controlled_buffer_4_out, controlled_buffer_6_out, controlled_buffer_7_out;
  wire [31:0] adder_1_out, multiplier_1_out, subtractor_1_out;

  Adder #(.width(32)) adder_1 (.a(A), .b(B), .out(adder_1_out));  // open: cin, cout
  Subtractor #(.width(32)) subtractor_1 (.a(A), .b(B), .out(subtractor_1_out));  // open: bin, bout
  Decoder #(.select(2)) decoder_1 (
    .out1(decoder_1_out1), .out2(decoder_1_out2), .out3(decoder_1_out3), .sel(MSEL), .en(1'b1));  // open: out0
  Multiplier #(.width(32)) multiplier_1 (.a(A), .b(B), .out(multiplier_1_out));  // open: cin, cout
  assign MOUT = decoder_1_out3 ? adder_1_out : 32'bz;  // Controlled_Buffer controlled_buffer_1
  assign MOUT = decoder_1_out2 ? subtractor_1_out : 32'bz;  // Controlled_Buffer controlled_buffer_2
  Comparator #(.width(32)) comparator_1 (
    .a(A), .b(B), .gt(comparator_1_gt), .eq(comparator_1_eq), .lt(comparator_1_lt));
  Decoder #(.select(2)) decoder_2 (
    .out0(decoder_2_out0), .out1(decoder_2_out1), .out2(decoder_2_out2), .out3(decoder_2_out3), .sel(GELSEL),
    .en(1'b1));
  assign MOUT = decoder_1_out1 ? multiplier_1_out : 32'bz;  // Controlled_Buffer controlled_buffer_3
  assign controlled_buffer_4_out = comparator_1_gt ? 2'b01 : 2'bz;  // Controlled_Buffer controlled_buffer_4
  assign GELOUT = decoder_2_out1 ? controlled_buffer_4_out : 2'bz;  // Controlled_Buffer controlled_buffer_5
  assign controlled_buffer_6_out = comparator_1_eq ? 2'b10 : 2'bz;  // Controlled_Buffer controlled_buffer_6
  assign controlled_buffer_7_out = comparator_1_lt ? 2'b11 : 2'bz;  // Controlled_Buffer controlled_buffer_7
  assign GELOUT = decoder_2_out2 ? controlled_buffer_6_out : 2'bz;  // Controlled_Buffer controlled_buffer_8
  assign GELOUT = decoder_2_out3 ? controlled_buffer_7_out : 2'bz;  // Controlled_Buffer controlled_buffer_9
  assign GELOUT = decoder_2_out0 ? 2'b00 : 2'bz;  // Controlled_Buffer controlled_buffer_10
endmodule

module CLU (
  input  [31:0] Ins,
  output NumIO,
  output RegAWR,
  output RegBWR,
  output MSELA,
  output MSELB,
  output GELSELA,
  output GELSELB,
  output ALUOUT,
  output PROCL,
  output RAMIOA,
  output RAMIOB,
  output GPIOA,
  output GPIOB,
  output EXINA,
  output EXINB,
  output EXINC,
  output EXIND,
  output out_19,
  output out_20,
  output out_21,
  output out_22,
  output out_23,
  output out_24,
  output out_25,
  output out_26,
  output out_27,
  output out_28,
  output out_29,
  output out_30,
  output out_31,
  output out_32,
  output out_33
);


  assign ALUOUT = Ins[7];
  assign EXINA = Ins[13];
  assign EXINB = Ins[14];
  assign EXINC = Ins[15];
  assign EXIND = Ins[16];
  assign GELSELA = Ins[5];
  assign GELSELB = Ins[6];
  assign GPIOA = Ins[11];
  assign GPIOB = Ins[12];
  assign MSELA = Ins[3];
  assign MSELB = Ins[4];
  assign NumIO = Ins[0];
  assign out_19 = Ins[17];
  assign out_20 = Ins[18];
  assign out_21 = Ins[19];
  assign out_22 = Ins[20];
  assign out_23 = Ins[21];
  assign out_24 = Ins[22];
  assign out_25 = Ins[23];
  assign out_26 = Ins[24];
  assign out_27 = Ins[25];
  assign out_28 = Ins[26];
  assign out_29 = Ins[27];
  assign out_30 = Ins[28];
  assign out_31 = Ins[29];
  assign out_32 = Ins[30];
  assign out_33 = Ins[31];
  assign PROCL = Ins[8];
  assign RAMIOA = Ins[9];
  assign RAMIOB = Ins[10];
  assign RegAWR = Ins[1];
  assign RegBWR = Ins[2];
endmodule
