// Logisim project O6_CPU.circ as structural Verilog: 9 circuits, main circuit main
module main (
);

  wire button_1_out, clock_1_out, clock_2_out, clock_3_out, cpu_1_gpwra;
  wire [1:0] cpu_1_ramsela, cpu_1_ramselb, cpu_1_ramselc, cpu_1_ramseld, ramcore_1_ramsel;
  wire [3:0] gpu_1_gpxa, gpu_1_gpxb, gpu_1_gpxc, gpu_1_gpxd, gpu_1_gpya, gpu_1_gpyb, gpu_1_gpyc, gpu_1_gpyd;
  wire [7:0] gpu_1_gpca, gpu_1_gpcb, gpu_1_gpcc, gpu_1_gpcd, gpuinterface_1_out_4, gpuinterface_1_out_5,
       gpuinterface_1_out_6, gpuinterface_1_out_7, gpuinterface_1_out_8, gpuinterface_1_out_9,
       gpuinterface_1_out_10, gpuinterface_1_out_11;
  wire [23:0] cpu_1_ramlinea, cpu_1_ramlineb, cpu_1_ramlinec, cpu_1_ramlined, ramcore_1_ramline;
  wire [31:0] cpu_1_gpda, cpu_1_gplna, cpu_1_ramouta, cpu_1_ramoutb, cpu_1_ramoutc, cpu_1_ramoutd,
       ramcore_1_ramout, ramcore_1_ramouta, ramcore_1_ramoutb, ramcore_1_ramoutc, ramcore_1_ramoutd,
       rammodule_1_ramout;

  BIOS bios_1 ();  // open: out_1, out_2, out_3, out_4, out_5, out_6, out_7, out_8, out_9, out_10, out_11, out_12
  Button button_1 (.out(button_1_out));
  Clock #(.highDuration(2), .lowDuration(2)) clock_1 (.out(clock_1_out));
  GPUInterface gpuinterface_1 (
    .GPWR(cpu_1_gpwra), .GPLN(cpu_1_gplna), .GPD(cpu_1_gpda), .out_4(gpuinterface_1_out_4),
    .out_5(gpuinterface_1_out_5), .out_6(gpuinterface_1_out_6), .out_7(gpuinterface_1_out_7),
    .out_8(gpuinterface_1_out_8), .out_9(gpuinterface_1_out_9), .out_10(gpuinterface_1_out_10),
    .out_11(gpuinterface_1_out_11));
  Clock #(.highDuration(4), .lowDuration(4)) clock_2 (.out(clock_2_out));
  CPU cpu_1 (
    .RAMInA(ramcore_1_ramoutd), .RAMInB(ramcore_1_ramoutc), .Clock(clock_2_out), .RAMInC(ramcore_1_ramoutb),
    .RAMInD(ramcore_1_ramouta), .RAMOutA(cpu_1_ramouta), .RAMLineA(cpu_1_ramlinea), .RAMSelA(cpu_1_ramsela),
    .GPDA(cpu_1_gpda), .GPLNA(cpu_1_gplna), .GPWRA(cpu_1_gpwra), .RAMOutB(cpu_1_ramoutb),
    .RAMLineB(cpu_1_ramlineb), .RAMSelB(cpu_1_ramselb), .RAMOutC(cpu_1_ramoutc), .RAMLineC(cpu_1_ramlinec),
    .RAMSelC(cpu_1_ramselc), .RAMOutD(cpu_1_ramoutd), .RAMLineD(cpu_1_ramlined), .RAMSelD(cpu_1_ramseld));  // open: BIOSINTLINEA, BIOSINTACA, BIOSINTDATA, BIOSINTLINEB, BIOSINTACB, BIOSINTDATB, BIOSINTLINEC, BIOSINTACC, BIOSINTDATC, BIOSINTLINED, BIOSINTACD, BIOSINTDATD, GPDB, GPLNB, GPWRB, GPDC, GPLNC, GPWRC, GPDD, GPLND, GPWRD
  GPU gpu_1 (
    .Clock(clock_1_out), .Reset(button_1_out), .GPLNA(gpuinterface_1_out_4), .GPLNB(gpuinterface_1_out_5),
    .GPINA(gpuinterface_1_out_6), .GPINB(gpuinterface_1_out_7), .GPLNC(gpuinterface_1_out_8),
    .GPLND(gpuinterface_1_out_9), .GPINC(gpuinterface_1_out_10), .GPIND(gpuinterface_1_out_11),
    .GPXA(gpu_1_gpxa), .GPXB(gpu_1_gpxb), .GPYA(gpu_1_gpya), .GPYB(gpu_1_gpyb), .GPCA(gpu_1_gpca),
    .GPCB(gpu_1_gpcb), .GPXC(gpu_1_gpxc), .GPXD(gpu_1_gpxd), .GPYC(gpu_1_gpyc), .GPYD(gpu_1_gpyd),
    .GPCC(gpu_1_gpcc), .GPCD(gpu_1_gpcd));
  // RGB_Video #(.cursor("No Cursor"), .height(16), .scale(8), .width(16)) rgb_video_1: pin names not known; wires that end beside it: button_1_out, clock_1_out, 1'b1, gpu_1_gpxa, gpu_1_gpya, gpu_1_gpca
  // RGB_Video #(.cursor("No Cursor"), .height(16), .scale(8), .width(16)) rgb_video_2: pin names not known; wires that end beside it: button_1_out, clock_1_out, 1'b1, gpu_1_gpxc, gpu_1_gpyc, gpu_1_gpcc
  // RGB_Video #(.cursor("No Cursor"), .height(16), .scale(8), .width(16)) rgb_video_3: pin names not known; wires that end beside it: button_1_out, clock_1_out, 1'b1, gpu_1_gpxb, gpu_1_gpyb, gpu_1_gpcb
  // RGB_Video #(.cursor("No Cursor"), .height(16), .scale(8), .width(16)) rgb_video_4: pin names not known; wires that end beside it: button_1_out, clock_1_out, 1'b1, gpu_1_gpxd, gpu_1_gpyd, gpu_1_gpcd
  RAMCore ramcore_1 (
    .RAMInA(cpu_1_ramouta), .RAMInB(cpu_1_ramoutb), .RAMInC(cpu_1_ramoutc), .RAMInD(cpu_1_ramoutd),
    .RAMLineA(cpu_1_ramlinea), .RAMLineB(cpu_1_ramlineb), .RAMLineC(cpu_1_ramlinec),
    .RAMLineD(cpu_1_ramlined), .RAMSelA(cpu_1_ramsela), .RAMSelB(cpu_1_ramselb), .RAMSelC(cpu_1_ramselc),
    .RAMSelD(cpu_1_ramseld), .RAMIn(rammodule_1_ramout), .Clock(clock_3_out), .RAMOutA(ramcore_1_ramouta),
    .RAMOutB(ramcore_1_ramoutb), .RAMOutC(ramcore_1_ramoutc), .RAMOutD(ramcore_1_ramoutd),
    .RAMSel(ramcore_1_ramsel), .RAMLine(ramcore_1_ramline), .RAMOut(ramcore_1_ramout));
  Clock clock_3 (.out(clock_3_out));
  RAMModule rammodule_1 (
    .RAMIn(ramcore_1_ramout), .RAMLine(ramcore_1_ramline), .RAMSel(ramcore_1_ramsel), .Clock(clock_3_out),
    .RAMOut(rammodule_1_ramout));
endmodule

module CPU (
  input  [31:0] RAMInA,
  input  [23:0] BIOSINTLINEA,
  input  BIOSINTACA,
  input  [63:0] BIOSINTDATA,
  input  [31:0] RAMInB,
  input  Clock,
  input  [23:0] BIOSINTLINEB,
  input  BIOSINTACB,
  input  [63:0] BIOSINTDATB,
  input  [31:0] RAMInC,
  input  [23:0] BIOSINTLINEC,
  input  BIOSINTACC,
  input  [63:0] BIOSINTDATC,
  input  [31:0] RAMInD,
  input  [23:0] BIOSINTLINED,
  input  BIOSINTACD,
  input  [63:0] BIOSINTDATD,
  output [31:0] RAMOutA,
  output [23:0] RAMLineA,
  output [1:0] RAMSelA,
  output [31:0] GPDA,
  output [31:0] GPLNA,
  output GPWRA,
  output [31:0] RAMOutB,
  output [23:0] RAMLineB,
  output [1:0] RAMSelB,
  output [31:0] GPDB,
  output [31:0] GPLNB,
  output GPWRB,
  output [31:0] RAMOutC,
  output [23:0] RAMLineC,
  output [1:0] RAMSelC,
  output [31:0] GPDC,
  output [31:0] GPLNC,
  output GPWRC,
  output [31:0] RAMOutD,
  output [23:0] RAMLineD,
  output [1:0] RAMSelD,
  output [31:0] GPDD,
  output [31:0] GPLND,
  output GPWRD
);

  CPUCore CoreA (
    .RAMIn(RAMInA), .Clock(Clock), .BIOSINTLINE(BIOSINTLINEA), .BIOSINTAC(BIOSINTACA),
    .BIOSINTDAT(BIOSINTDATA), .RAMOut(RAMOutA), .RAMLine(RAMLineA), .RAMSel(RAMSelA), .GPD(GPDA),
    .GPLN(GPLNA), .GPWR(GPWRA));
  CPUCore CoreB (
    .RAMIn(RAMInB), .Clock(Clock), .BIOSINTLINE(BIOSINTLINEB), .BIOSINTAC(BIOSINTACB),
    .BIOSINTDAT(BIOSINTDATB), .RAMOut(RAMOutB), .RAMLine(RAMLineB), .RAMSel(RAMSelB), .GPD(GPDB),
    .GPLN(GPLNB), .GPWR(GPWRB));
  CPUCore CoreC (
    .RAMIn(RAMInC), .Clock(Clock), .BIOSINTLINE(BIOSINTLINEC), .BIOSINTAC(BIOSINTACC),
    .BIOSINTDAT(BIOSINTDATC), .RAMOut(RAMOutC), .RAMLine(RAMLineC), .RAMSel(RAMSelC), .GPD(GPDC),
    .GPLN(GPLNC), .GPWR(GPWRC));
  CPUCore CoreD (
    .RAMIn(RAMInD), .Clock(Clock), .BIOSINTLINE(BIOSINTLINED), .BIOSINTAC(BIOSINTACD),
    .BIOSINTDAT(BIOSINTDATD), .RAMOut(RAMOutD), .RAMLine(RAMLineD), .RAMSel(RAMSelD), .GPD(GPDD),
    .GPLN(GPLND), .GPWR(GPWRD));
endmodule

module ALU (
  input  [31:0] A,
  input  [31:0] B,
  input  [2:0] SEL,
  input  Clock,
  input  RNGE,
  output [31:0] MOUT,
  output GEL,
  output [31:0] RNGOut
);

  wire comparator_1_eq, comparator_1_gt, comparator_1_lt, demultiplexer_1_out0, demultiplexer_1_out1,
       demultiplexer_1_out2, demultiplexer_1_out3, demultiplexer_1_out4, demultiplexer_1_out5,
       demultiplexer_1_out6, demultiplexer_1_out7, not_1_out, xnor_1_out, xor_1_out;
  wire [31:0] adder_1_out, controlled_buffer_1_out, controlled_buffer_2_out, multiplier_1_out,
       subtractor_1_out;

  Demultiplexer #(.select(3)) demultiplexer_1 (
    .out0(demultiplexer_1_out0), .out1(demultiplexer_1_out1), .out2(demultiplexer_1_out2),
    .out3(demultiplexer_1_out3), .out4(demultiplexer_1_out4), .out5(demultiplexer_1_out5),
    .out6(demultiplexer_1_out6), .out7(demultiplexer_1_out7), .in(1'b1), .sel(SEL));
  assign controlled_buffer_1_out = demultiplexer_1_out0 ? {32{1'b0}} : 32'bz;  // Controlled_Buffer controlled_buffer_1
  assign controlled_buffer_2_out = not_1_out ? B : 32'bz;  // Controlled_Buffer controlled_buffer_2
  not not_1 (not_1_out, demultiplexer_1_out4);
  assign controlled_buffer_2_out = demultiplexer_1_out4 ? controlled_buffer_1_out : 32'bz;  // Controlled_Buffer controlled_buffer_3
  assign controlled_buffer_1_out = demultiplexer_1_out1 ? subtractor_1_out : 32'bz;  // Controlled_Buffer controlled_buffer_4
  Subtractor #(.width(32)) subtractor_1 (.a(A), .b(B), .out(subtractor_1_out));  // open: bin, bout
  assign controlled_buffer_1_out = demultiplexer_1_out2 ? adder_1_out : 32'bz;  // Controlled_Buffer controlled_buffer_5
  Adder #(.width(32)) adder_1 (.a(A), .b(B), .out(adder_1_out));  // open: cin, cout
  Multiplier #(.mode("twosComplement"), .width(32)) multiplier_1 (
    .a(A), .b(B), .out(multiplier_1_out));  // open: cin, cout
  assign GEL = xor_1_out ? 1'b0 : 1'bz;  // Controlled_Buffer controlled_buffer_6
  Comparator #(.width(32)) comparator_1 (
    .a(A), .b(controlled_buffer_2_out), .gt(comparator_1_gt), .eq(comparator_1_eq), .lt(comparator_1_lt));
  Random #(.width(32)) random_1 (.next(RNGE), .clk(Clock), .out(RNGOut));  // open: clr
  assign controlled_buffer_1_out = demultiplexer_1_out3 ? multiplier_1_out : 32'bz;  // Controlled_Buffer controlled_buffer_7
  assign GEL = demultiplexer_1_out5 ? comparator_1_gt : 1'bz;  // Controlled_Buffer controlled_buffer_8
  assign GEL = demultiplexer_1_out6 ? comparator_1_eq : 1'bz;  // Controlled_Buffer controlled_buffer_9
  assign GEL = demultiplexer_1_out7 ? comparator_1_lt : 1'bz;  // Controlled_Buffer controlled_buffer_10
  assign MOUT = Clock ? controlled_buffer_1_out : 32'bz;  // Controlled_Buffer controlled_buffer_11
  xnor xnor_1 (xnor_1_out, demultiplexer_1_out6, demultiplexer_1_out7);
  xor xor_1 (xor_1_out, demultiplexer_1_out5, xnor_1_out);
endmodule

module CLU (
  input  [63:0] IntIn,
  output [31:0] IntNum,
  output Num,
  output RegAWR,
  output RegBWR,
  output ALUSecSel,
  output [2:0] ALUSel,
  output [1:0] RAMSel,
  output RegARAM,
  output RegBRAM,
  output ProcRAM,
  output ProcWR,
  output RNGStep,
  output RAMOutBus,
  output RAMOutRAM,
  output ALUOut,
  output RAMOutWR,
  output RAMLineWR,
  output RNGOut,
  output GPOutBus,
  output GPOutWR,
  output GPLineWR,
  output GPWR
);


  assign ALUOut = IntIn[16];
  assign ALUSecSel = IntIn[3];
  assign ALUSel = IntIn[6:4];
  assign GPLineWR = IntIn[22];
  assign GPOutBus = IntIn[20];
  assign GPOutWR = IntIn[21];
  assign GPWR = IntIn[23];
  assign IntNum = IntIn[63:32];
  assign Num = IntIn[0];
  assign ProcRAM = IntIn[11];
  assign ProcWR = IntIn[12];
  assign RAMLineWR = IntIn[18];
  assign RAMOutBus = IntIn[14];
  assign RAMOutRAM = IntIn[15];
  assign RAMOutWR = IntIn[17];
  assign RAMSel = IntIn[8:7];
  assign RegARAM = IntIn[9];
  assign RegAWR = IntIn[1];
  assign RegBRAM = IntIn[10];
  assign RegBWR = IntIn[2];
  assign RNGOut = IntIn[19];
  assign RNGStep = IntIn[13];
endmodule

module CPUCore (
  input  [31:0] RAMIn,
  input  Clock,
  input  [23:0] BIOSINTLINE,
  input  BIOSINTAC,
  input  [63:0] BIOSINTDAT,
  output [31:0] RAMOut,
  output [23:0] RAMLine,
  output [1:0] RAMSel,
  output [31:0] GPD,
  output [31:0] GPLN,
  output GPWR
);

  wire alu_1_gel, clu_1_aluout, clu_1_alusecsel, clu_1_gplinewr, clu_1_gpoutbus, clu_1_gpoutwr, clu_1_num,
       clu_1_procram, clu_1_procwr, clu_1_ramlinewr, clu_1_ramoutbus, clu_1_ramoutram, clu_1_ramoutwr,
       clu_1_regaram, clu_1_regawr, clu_1_regbram, clu_1_regbwr, clu_1_rngout, clu_1_rngstep, not_1_out,
       not_2_out, not_3_out;
  wire [2:0] clu_1_alusel;
  wire [7:0] controlled_buffer_4_out_2, controlled_buffer_12_out_2;
  wire [23:0] controlled_buffer_1_out, controlled_buffer_4_out, controlled_buffer_12_out, counter_1_q;
  wire [31:0] A_q, alu_1_mout, alu_1_rngout, B_q, buffer_1_out, buffer_3_out, clu_1_intnum,
       controlled_buffer_3_out, controlled_buffer_6_out, controlled_buffer_8_out, controlled_buffer_11_out,
       controlled_buffer_14_out;
  wire [63:0] ram_1_dout;

  assign controlled_buffer_1_out = not_1_out ? counter_1_q : 24'bz;  // Controlled_Buffer controlled_buffer_1
  assign controlled_buffer_1_out = BIOSINTAC ? BIOSINTLINE : 24'bz;  // Controlled_Buffer controlled_buffer_2
  RAM #(.addrWidth(24), .dataWidth(64)) ram_1 (
    .addr(controlled_buffer_1_out), .we(BIOSINTAC), .oe(1'b1), .clk(Clock), .din(BIOSINTDAT),
    .dout(ram_1_dout));
  not not_1 (not_1_out, BIOSINTAC);
  Counter #(.max('hffffff), .width(24)) counter_1 (
    .load(alu_1_gel), .up(1'b1), .count(1'b1), .clk(Clock), .D(controlled_buffer_4_out), .Q(counter_1_q));  // open: clr, carry
  assign controlled_buffer_3_out = clu_1_regbram ? RAMIn : 32'bz;  // Controlled_Buffer controlled_buffer_3
  CLU clu_1 (
    .IntIn(ram_1_dout), .IntNum(clu_1_intnum), .Num(clu_1_num), .RegAWR(clu_1_regawr), .RegBWR(clu_1_regbwr),
    .ALUSecSel(clu_1_alusecsel), .ALUSel(clu_1_alusel), .RAMSel(RAMSel), .RegARAM(clu_1_regaram),
    .RegBRAM(clu_1_regbram), .ProcRAM(clu_1_procram), .ProcWR(clu_1_procwr), .RNGStep(clu_1_rngstep),
    .RAMOutBus(clu_1_ramoutbus), .RAMOutRAM(clu_1_ramoutram), .ALUOut(clu_1_aluout),
    .RAMOutWR(clu_1_ramoutwr), .RAMLineWR(clu_1_ramlinewr), .RNGOut(clu_1_rngout), .GPOutBus(clu_1_gpoutbus),
    .GPOutWR(clu_1_gpoutwr), .GPLineWR(clu_1_gplinewr), .GPWR(GPWR));
  assign {controlled_buffer_4_out_2, controlled_buffer_4_out} = clu_1_procwr ? buffer_1_out : 32'bz;  // Controlled_Buffer controlled_buffer_4
  assign buffer_1_out = controlled_buffer_3_out;  // Buffer buffer_1, 32 bits wide
  assign buffer_1_out = clu_1_procram ? RAMIn : 32'bz;  // Controlled_Buffer controlled_buffer_5
  assign controlled_buffer_6_out = clu_1_regaram ? RAMIn : 32'bz;  // Controlled_Buffer controlled_buffer_6
  assign controlled_buffer_3_out = clu_1_num ? clu_1_intnum : 32'bz;  // Controlled_Buffer controlled_buffer_7
  Register #(.width(32)) A (.D(controlled_buffer_6_out), .en(clu_1_regawr), .clk(Clock), .Q(A_q));  // open: clr
  assign controlled_buffer_6_out = controlled_buffer_3_out;  // Buffer buffer_2, 32 bits wide
  assign buffer_3_out = controlled_buffer_3_out;  // Buffer buffer_3, 32 bits wide
  Register #(.width(32)) B (.D(buffer_3_out), .en(clu_1_regbwr), .clk(Clock), .Q(B_q));  // open: clr
  assign controlled_buffer_8_out = clu_1_alusecsel ? B_q : 32'bz;  // Controlled_Buffer controlled_buffer_8
  assign controlled_buffer_8_out = not_2_out ? controlled_buffer_3_out : 32'bz;  // Controlled_Buffer controlled_buffer_9
  not not_2 (not_2_out, clu_1_alusecsel);
  assign controlled_buffer_3_out = clu_1_aluout ? alu_1_mout : 32'bz;  // Controlled_Buffer controlled_buffer_10
  ALU alu_1 (
    .A(A_q), .B(controlled_buffer_8_out), .SEL(clu_1_alusel), .Clock(Clock), .RNGE(clu_1_rngstep),
    .MOUT(alu_1_mout), .GEL(alu_1_gel), .RNGOut(alu_1_rngout));
  not not_3 (not_3_out, clu_1_ramoutram);
  assign controlled_buffer_11_out = not_3_out ? RAMIn : 32'bz;  // Controlled_Buffer controlled_buffer_11
  assign controlled_buffer_11_out = {controlled_buffer_12_out_2, controlled_buffer_12_out};  // Buffer buffer_4, 32 bits wide
  assign {controlled_buffer_12_out_2, controlled_buffer_12_out} = clu_1_ramoutbus ? controlled_buffer_3_out : 32'bz;  // Controlled_Buffer controlled_buffer_12
  assign controlled_buffer_3_out = clu_1_rngout ? alu_1_rngout : 32'bz;  // Controlled_Buffer controlled_buffer_13
  Register #(.width(32)) RAMReg (
    .D(controlled_buffer_11_out), .en(clu_1_ramoutwr), .clk(Clock), .Q(RAMOut));  // open: clr
  Register #(.width(24)) RAMLReg (
    .D(controlled_buffer_12_out), .en(clu_1_ramlinewr), .clk(Clock), .Q(RAMLine));  // open: clr
  assign controlled_buffer_14_out = clu_1_gpoutbus ? controlled_buffer_3_out : 32'bz;  // Controlled_Buffer controlled_buffer_14
  Register #(.width(32)) GPReg (.D(controlled_buffer_14_out), .en(clu_1_gpoutwr), .clk(Clock), .Q(GPD));  // open: clr
  Register #(.width(32)) GPLReg (
    .D(controlled_buffer_14_out), .en(clu_1_gplinewr), .clk(Clock), .Q(GPLN));  // open: clr
endmodule

module RAMCore (
  input  [31:0] RAMInA,
  input  [31:0] RAMInB,
  input  [31:0] RAMInC,
  input  [31:0] RAMInD,
  input  [23:0] RAMLineA,
  input  [23:0] RAMLineB,
  input  [23:0] RAMLineC,
  input  [23:0] RAMLineD,
  input  [1:0] RAMSelA,
  input  [1:0] RAMSelB,
  input  [1:0] RAMSelC,
  input  [1:0] RAMSelD,
  input  [31:0] RAMIn,
  input  Clock,
  output [31:0] RAMOutA,
  output [31:0] RAMOutB,
  output [31:0] RAMOutC,
  output [31:0] RAMOutD,
  output [1:0] RAMSel,
  output [23:0] RAMLine,
  output [31:0] RAMOut
);

  wire demultiplexer_2_out0, demultiplexer_2_out1, demultiplexer_2_out2, demultiplexer_2_out3;
  wire [1:0] counter_1_q;
  wire [31:0] demultiplexer_1_out0, demultiplexer_1_out1, demultiplexer_1_out2, demultiplexer_1_out3;

  Counter #(.max('h3), .width(2)) counter_1 (
    .up(1'b1), .count(1'b1), .clk(Clock), .Q(counter_1_q));  // open: clr, load, D, carry
  Multiplexer #(.select(2), .width(24)) multiplexer_1 (
    .in0(RAMLineA), .in1(RAMLineB), .in2(RAMLineC), .in3(RAMLineD), .out(RAMLine), .sel(counter_1_q));
  Multiplexer #(.select(2), .width(2)) multiplexer_2 (
    .in0(RAMSelA), .in1(RAMSelB), .in2(RAMSelC), .in3(RAMSelD), .out(RAMSel), .sel(counter_1_q));
  Demultiplexer #(.select(2), .width(32)) demultiplexer_1 (
    .out0(demultiplexer_1_out0), .out1(demultiplexer_1_out1), .out2(demultiplexer_1_out2),
    .out3(demultiplexer_1_out3), .in(RAMIn), .sel(counter_1_q));
  Multiplexer #(.select(2), .width(32)) multiplexer_3 (
    .in0(RAMInA), .in1(RAMInB), .in2(RAMInC), .in3(RAMInD), .out(RAMOut), .sel(counter_1_q));
  Demultiplexer #(.select(2)) demultiplexer_2 (
    .out0(demultiplexer_2_out0), .out1(demultiplexer_2_out1), .out2(demultiplexer_2_out2),
    .out3(demultiplexer_2_out3), .in(1'b1), .sel(counter_1_q));
  Register #(.width(32)) register_1 (
    .D(demultiplexer_1_out0), .en(demultiplexer_2_out0), .clk(Clock), .Q(RAMOutA));  // open: clr
  Register #(.width(32)) register_2 (
    .D(demultiplexer_1_out1), .en(demultiplexer_2_out1), .clk(Clock), .Q(RAMOutB));  // open: clr
  Register #(.width(32)) register_3 (
    .D(demultiplexer_1_out2), .en(demultiplexer_2_out2), .clk(Clock), .Q(RAMOutC));  // open: clr
  Register #(.width(32)) register_4 (
    .D(demultiplexer_1_out3), .en(demultiplexer_2_out3), .clk(Clock), .Q(RAMOutD));  // open: clr
endmodule

module RAMModule (
  input  [31:0] RAMIn,
  input  [23:0] RAMLine,
  input  [1:0] RAMSel,
  input  Clock,
  output [31:0] RAMOut
);

  RAM #(.addrWidth(24), .dataWidth(32)) ram_1 (
    .addr(RAMLine), .we(RAMSel[0]), .oe(RAMSel[1]), .clk(Clock), .din(RAMIn), .dout(RAMOut));
endmodule

module GPUInterface (
  input  GPWR,
  input  [31:0] GPLN,
  input  [31:0] GPD,
  output [7:0] out_4,
  output [7:0] out_5,
  output [7:0] out_6,
  output [7:0] out_7,
  output [7:0] out_8,
  output [7:0] out_9,
  output [7:0] out_10,
  output [7:0] out_11
);

  wire not_1_out;

  assign {out_11, out_10, out_7, out_6} = GPWR ? GPD : 32'bz;  // Controlled_Buffer controlled_buffer_1
  not not_1 (not_1_out, GPWR);
  assign {out_9, out_8, out_5, out_4} = GPWR ? GPLN : 32'bz;  // Controlled_Buffer controlled_buffer_2
  assign out_11 = not_1_out ? {8{1'b0}} : 8'bz;  // Controlled_Buffer controlled_buffer_3
  assign out_10 = not_1_out ? {8{1'b0}} : 8'bz;  // Controlled_Buffer controlled_buffer_4
  assign out_9 = not_1_out ? {8{1'b0}} : 8'bz;  // Controlled_Buffer controlled_buffer_5
  assign out_8 = not_1_out ? {8{1'b0}} : 8'bz;  // Controlled_Buffer controlled_buffer_6
  assign out_7 = not_1_out ? {8{1'b0}} : 8'bz;  // Controlled_Buffer controlled_buffer_7
  assign out_6 = not_1_out ? {8{1'b0}} : 8'bz;  // Controlled_Buffer controlled_buffer_8
  assign out_5 = not_1_out ? {8{1'b0}} : 8'bz;  // Controlled_Buffer controlled_buffer_9
  assign out_4 = not_1_out ? {8{1'b0}} : 8'bz;  // Controlled_Buffer controlled_buffer_10
endmodule

module BIOS (
  output out_1,
  output out_2,
  output out_3,
  output out_4,
  output out_5,
  output out_6,
  output out_7,
  output out_8,
  output out_9,
  output out_10,
  output out_11,
  output out_12
);
endmodule
